# Fritzing sketch PCB v.2.0 19Jun26 (saved by Fritzing 1.0.6)
circuit board: 2.37cm x 1.87cm
breadboards: 1

parts:
  5V3 = Diode [package=diode-1n4148]
  th2 = Dagu DGServo 9g header (male) [package=THT]
  th3 = Dagu DGServo 9g header (male) [package=THT]
  5V4 = Diode [package=diode-1n4148]

nets:
  N1: 5V3.A, 5V4.A
  GND: th2.gnd, th3.gnd, 5V4.C
  VCC: th2.Vcc, th3.Vcc

notes:
  OpenRC4CL V2.0
  R1
  R2
  19Jun26
  chan1    ESC
  BP -        SW1/2TH
  -Bat+
  - + S     - + S
  jmp
  D6 D5  D4 D3  A2  A1 A0
  D7 D8  D9 D10      -
  3V
  5V
