# Fritzing sketch PCB v1.0 31Mar26 (saved by Fritzing 1.0.6)
circuit board: 3.90129cm x 1.86578cm
breadboards: 1

parts:
  5V = Diode [package=diode-1n4148]
  J7 = Dagu DGServo 9g header (male) [package=THT]
  J9 = Dagu DGServo 9g header (male) [package=THT]
  J10 = Dagu DGServo 9g header (male) [package=THT]
  th1 = Dagu DGServo 9g header (male) [package=THT]
  5V1 = Diode [package=diode-1n4148]
  5V2 = Diode [package=diode-1n4148]

nets:
  VCC: 5V.A, J7.Vcc, J9.Vcc, J10.Vcc, th1.Vcc
  GND: J7.gnd, J9.gnd, J10.gnd, th1.gnd, 5V1.A
  N1: 5V1.C, 5V2.C

notes:
  OpenRC4CL V1.0
  R1
  R2
  TH D6 D5 D4 D3 A2 A1 A0
  BP D7 D8 D9D10 3V - 5V
  SWL/R
  -VBat+
  -+s
  C3
  C2
  31Mar26
  D1
  ESC
  C1
