# Fritzing sketch Rx-1 (saved by Fritzing 1.0.6)
breadboards: 1

parts:
  U1 = XIAO ESP32C6 [part_number=" XIAO ESP32C6"]
  SW1 = DIP SWITCH [package=dipswitch-02]
  U2 = Hirose DF13 Series Header [part_number=DF13#-2P-1.25V package=DF13C-2P-1.25V]
  R1 = Resistor [tolerance=±5% power=0.25W resistance=100k package=THT]
  R2 = Resistor [tolerance=±5% power=0.25W resistance=10k package=THT]
  D1 = Rectifier Diode [part_number=1N4001 mn=ss package="300 mil [THT]"]
  R3 = 12mm Trimmer Potentiometer (Large) [maximum_resistance=10kΩ knob_status=50% power=0.5W package=THT]

nets:
  N1: U1.D1, R3.wiper
  N2: U1.D2, R1.Pin_1, R2.Pin_1
  N3: U1.D9, SW1.4
  N4: U1.D10, SW1.3
  N5: U1.3V3, R3.leg2
  N6: U1.GND, SW1.1, SW1.2, R2.Pin_0
  N7: U1.5V, D1.cathode
  N8: U2.1, R1.Pin_0
  N9: U2.2, R3.leg1

notes:
  S + -
  - +

custom parts:
  XIAO ESP32C6: XIAO ESP32C6 is a cost-effective MCU based on Espressif’s ESP32-C6. This compact MCU excels in Matter-compliant smart home applications with its support for various wireless connectivity (2.4GHz Wi-Fi 6, BLE 5.0, Zigbee, and Thread). Designed with the thumb-size footprint and a single-sided mount of the XIAO Series, it's perfect for space-limited projects. Encrypted on the chip, the XIAO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
